# Fritzing sketch usb_modbus (saved by Fritzing 0.9.4)

parts:
  MODBUS = RS485 Module (MAX3485)
  DMX = RS485 Module (MAX3485)
  LED1 = smd LED [color="Red (633nm)" package="0603 [SMD]"]
  J1 = Screw terminal - 2 pins [package=THT]
  J2 = Screw terminal - 2 pins [package=THT]
  Компонент1 = Arduino Mega 2560 (Rev3)
  D1 = LED_BARGRAPH_10 [package=led_bargaph_10]
  SW1 = DIP Switch 8 Position [package=dipswitch-08]

nets:
  GND: MODBUS.GND, DMX.GND, LED1.cathode, Компонент1.GND, D1.I_C, D1.H_C, D1.G_C, D1.F_C
  N1: MODBUS.A, J2.pin1
  N2: MODBUS.B, J2.pin2
  VCC: MODBUS.VCC, DMX.VCC, Компонент1.5V, SW1.9, SW1.10, SW1.11, SW1.12, SW1.13, SW1.14, SW1.15, SW1.16
  N3: MODBUS.RO, Компонент1.D17_PWM/RX2
  N4: MODBUS.RE, Компонент1.3V3
  N5: MODBUS.DE, Компонент1.D4_PWM
  N6: MODBUS.DI, Компонент1.D16_PWM/TX2
  N7: DMX.A, J1.pin1
  N8: DMX.B, J1.pin2
  N9: DMX.RO, Компонент1.D19/RX1
  N10: DMX.RE, Компонент1.D3_PWM
  N11: DMX.DE, Компонент1.D2_PWM
  N12: DMX.DI, Компонент1.D18/TX1
  N13: LED1.anode, Компонент1.D11_PWM
  N14: Компонент1.D10_PWM, D1.F_A
  N15: Компонент1.D9_PWM, D1.G_A
  N16: Компонент1.D5_PWM, D1.I_A
  N17: Компонент1.D6_PWM, D1.H_A
  N18: Компонент1.D22, SW1.1
  N19: Компонент1.D24, SW1.2
  N20: Компонент1.D26, SW1.3
  N21: Компонент1.D28, SW1.4
  N22: Компонент1.D30, SW1.5
  N23: Компонент1.D32, SW1.6
  N24: Компонент1.D34, SW1.7
  N25: Компонент1.D36, SW1.8

notes:
  Принимаем сигнал по DMX и отправляем по MODBUS

custom parts:
  RS485 Module (MAX3485): Commercially available RS485 to RS232 TTL Module
